// Logisim project ALU.circ as structural Verilog: 6 circuits, main circuit ALU
module ALU (
  input  [5:0] Operation,
  input  [31:0] A,
  input  [31:0] B,
  output [31:0] Result
);

  wire N, V, Z;
  wire [31:0] A_t, arithmaticunit_1_arithmatic, B_t, compareunit_1_compare, logicunit_1_logic, not_1_out,
       not_2_out, shiftunit_1_shift;

  Multiplexer #(.width(32)) multiplexer_1 (.in0(A), .in1(not_1_out), .out(A_t), .sel(Operation[5]));
  assign not_1_out = ~A;  // NOT_Gate not_1, 32 bits wide
  Multiplexer #(.width(32)) multiplexer_2 (.in0(B), .in1(not_2_out), .out(B_t), .sel(Operation[4]));
  assign not_2_out = ~B;  // NOT_Gate not_2, 32 bits wide
  CompareUnit compareunit_1 (.Z(Z), .V(V), .N(N), .Operation(Operation[1:0]), .Compare(compareunit_1_compare));
  ArithmaticUnit arithmaticunit_1 (
    .A(A_t), .B(B_t), .Cin(Operation[4]), .Arithmatic(arithmaticunit_1_arithmatic), .Z(Z), .V(V), .N(N));
  LogicUnit logicunit_1 (.A(A_t), .B(B_t), .Operation(Operation[1:0]), .Logic(logicunit_1_logic));
  ShiftUnit shiftunit_1 (.A(A_t), .B(B[4:0]), .Operation(Operation[1:0]), .Shift(shiftunit_1_shift));
  Multiplexer #(.select(2), .width(32)) multiplexer_3 (
    .in0(compareunit_1_compare), .in1(arithmaticunit_1_arithmatic), .in2(logicunit_1_logic),
    .in3(shiftunit_1_shift), .out(Result), .sel(Operation[3:2]));

  // Other names for the same wires on the sheet: ShiftB[4:0] = B[4:0]; nB = Operation[4]; nA = Operation[5];
  //   Operation_t[1:0] = Operation[3:2]; SubOperation[1:0] = Operation[1:0]
endmodule

module ShiftUnit (
  input  [31:0] A,
  input  [4:0] B,
  input  [1:0] Operation,
  output [31:0] Shift
);

  wire [31:0] shifter_1_out, shifter_2_out, shifter_3_out;

  Shifter #(.width(32)) shifter_1 (.in(A), .\dist (B), .out(shifter_1_out));
  Shifter #(.shift("lr"), .width(32)) shifter_2 (.in(A), .\dist (B), .out(shifter_2_out));
  Shifter #(.shift("ar"), .width(32)) shifter_3 (.in(A), .\dist (B), .out(shifter_3_out));
  Multiplexer #(.select(2), .width(32)) multiplexer_1 (
    .in0(shifter_1_out), .in1(shifter_2_out), .in3(shifter_3_out), .out(Shift), .sel(Operation));  // open: in2
endmodule

module LogicUnit (
  input  [31:0] A,
  input  [31:0] B,
  input  [1:0] Operation,
  output [31:0] Logic
);

  wire [31:0] and_1_out, or_1_out, xor_1_out;

  assign and_1_out = A & B;  // AND_Gate and_1, 32 bits wide
  assign or_1_out = A | B;  // OR_Gate or_1, 32 bits wide
  assign xor_1_out = A ^ B;  // XOR_Gate xor_1, 32 bits wide
  Multiplexer #(.select(2), .width(32)) multiplexer_1 (
    .in0(and_1_out), .in1(or_1_out), .in3(xor_1_out), .out(Logic), .sel(Operation));  // open: in2
endmodule

module ArithmaticUnit (
  input  [31:0] A,
  input  [31:0] B,
  input  Cin,
  output [31:0] Arithmatic,
  output Z,
  output V,
  output N
);

  wire and_1_out, and_2_out, nor_1_out, not_1_out, not_2_out, not_3_out;

  not not_1 (not_1_out, Arithmatic[31]);
  and and_1 (and_1_out, B[31], A[31], not_1_out);
  not not_2 (not_2_out, B[31]);
  not not_3 (not_3_out, A[31]);
  and and_2 (and_2_out, not_2_out, not_3_out, Arithmatic[31]);
  nor nor_1 (nor_1_out, A[31], Arithmatic[31]);
  Adder #(.width(32)) adder_1 (.a(A), .b(B), .out(Arithmatic), .cin(Cin));  // open: cout
  ZeroDetector zerodetector_1 (.Di(Arithmatic), .Do(Z));
  or or_1 (V, and_2_out, nor_1_out, and_1_out);

  assign N = Arithmatic[31];
endmodule

module CompareUnit (
  input  Z,
  input  V,
  input  N,
  input  [1:0] Operation,
  output [31:0] Compare
);

  wire or_1_out, xor_1_out;

  xor xor_1 (xor_1_out, V, N);
  Multiplexer #(.select(2)) multiplexer_1 (
    .in1(Z), .in2(xor_1_out), .in3(or_1_out), .out(Compare[0]), .sel(Operation));  // open: in0
  or or_1 (or_1_out, Z, xor_1_out);

  assign Compare[31:1] = {31{1'b0}};
endmodule

// Zero Detector
module ZeroDetector (
  input  [31:0] Di,
  output Do
);

  wire or_1_out;

  or or_1 (or_1_out, Di[0], Di[1], Di[2], Di[3], Di[4], Di[5], Di[6], Di[7], Di[8], Di[9], Di[10], Di[11], Di[12], Di[13], Di[14], Di[15], Di[16], Di[17], Di[18], Di[19], Di[20], Di[21], Di[22], Di[23], Di[24], Di[25], Di[26], Di[27], Di[28], Di[29], Di[30], Di[31]);
  not not_1 (Do, or_1_out);
endmodule
