// Logisim project CPU.circ as structural Verilog: 3 circuits, main circuit main
module main (
  input  [31:0] Instruction
);

  wire AluSrc, C, MemToReg, MemWrite, undriven_2;
  wire [4:0] undriven_3, undriven_5, undriven_6;
  wire [5:0] undriven;
  wire [31:0] ALU, MemOut, multiplexer_1_out, multiplexer_2_out, registers_1_rs1val, Rs2Val, undriven_4;

  // InstructionDecoder_Control instructiondecoder_control_1: pin names not known
  Multiplexer #(.width(32)) multiplexer_1 (.in0(ALU), .in1(MemOut), .out(multiplexer_1_out), .sel(MemToReg));
  Registers registers_1 (
    .Rs1(undriven_5), .Rs2(undriven_6), .En(undriven_2), .Rd(undriven_3), .Data_In(multiplexer_1_out), .C(C),
    .Rs1Val(registers_1_rs1val), .Rs2Val(Rs2Val));
  Multiplexer #(.width(32)) multiplexer_2 (.in0(Rs2Val), .in1(undriven_4), .out(multiplexer_2_out), .sel(AluSrc));
  ALU alu_1 (.Operation(undriven), .A(registers_1_rs1val), .B(multiplexer_2_out), .Result(ALU));
  RAM #(.addrWidth(24), .dataWidth(32), .enables("line")) ram_1 (
    .addr(ALU[23:0]), .we(MemWrite), .clk(C), .din(Rs2Val), .dout(MemOut));
endmodule

module BigRam (
  input  [31:0] DIn,
  input  [31:0] Address,
  input  En,
  input  C,
  output [31:0] DOut
);

  wire controlled_buffer_2_out, controlled_buffer_4_out, controlled_buffer_6_out, controlled_buffer_8_out,
       controlled_buffer_10_out, controlled_buffer_12_out, controlled_buffer_14_out,
       controlled_buffer_15_out, demultiplexer_1_out0, demultiplexer_1_out1, demultiplexer_2_out0,
       demultiplexer_2_out1, demultiplexer_2_out2, demultiplexer_2_out3, demultiplexer_2_out4,
       demultiplexer_2_out5, demultiplexer_2_out6, demultiplexer_2_out7;
  wire [23:0] controlled_buffer_1_out, controlled_buffer_3_out, controlled_buffer_5_out,
       controlled_buffer_7_out, controlled_buffer_9_out, controlled_buffer_11_out, controlled_buffer_13_out,
       controlled_buffer_16_out;
  wire [31:0] multiplexer_1_out, multiplexer_2_out, ram_1_dout, ram_2_dout, ram_3_dout, ram_4_dout,
       ram_5_dout, ram_6_dout, ram_7_dout, ram_8_dout;

  Demultiplexer demultiplexer_1 (
    .out0(demultiplexer_1_out0), .out1(demultiplexer_1_out1), .in(1'b1), .sel(Address[29]));
  Demultiplexer #(.select(5)) demultiplexer_2 (
    .out0(demultiplexer_2_out0), .out1(demultiplexer_2_out1), .out2(demultiplexer_2_out2),
    .out3(demultiplexer_2_out3), .out4(demultiplexer_2_out4), .out5(demultiplexer_2_out5),
    .out6(demultiplexer_2_out6), .out7(demultiplexer_2_out7), .in(demultiplexer_1_out0), .sel(Address[28:24]));  // open: out8, out9, out10, out11, out12, out13, out14, out15, out16, out17, out18, out19, out20, out21, out22, out23, out24, out25, out26, out27, out28, out29, out30, out31
  Demultiplexer #(.select(5)) demultiplexer_3 (
    .in(demultiplexer_1_out1), .sel(Address[28:24]));  // open: out0, out1, out2, out3, out4, out5, out6, out7, out8, out9, out10, out11, out12, out13, out14, out15, out16, out17, out18, out19, out20, out21, out22, out23, out24, out25, out26, out27, out28, out29, out30, out31
  RAM #(.addrWidth(24), .dataWidth(32), .enables("line")) ram_1 (
    .addr(controlled_buffer_1_out), .we(controlled_buffer_2_out), .clk(C), .din(DIn), .dout(ram_1_dout));
  assign controlled_buffer_1_out = demultiplexer_2_out0 ? Address[23:0] : 24'bz;  // Controlled_Buffer controlled_buffer_1
  assign controlled_buffer_2_out = demultiplexer_2_out0 ? En : 1'bz;  // Controlled_Buffer controlled_buffer_2
  RAM #(.addrWidth(24), .dataWidth(32), .enables("line")) ram_2 (
    .addr(controlled_buffer_3_out), .we(controlled_buffer_4_out), .clk(C), .din(DIn), .dout(ram_2_dout));
  assign controlled_buffer_3_out = demultiplexer_2_out1 ? Address[23:0] : 24'bz;  // Controlled_Buffer controlled_buffer_3
  assign controlled_buffer_4_out = demultiplexer_2_out1 ? En : 1'bz;  // Controlled_Buffer controlled_buffer_4
  RAM #(.addrWidth(24), .dataWidth(32), .enables("line")) ram_3 (
    .addr(controlled_buffer_5_out), .we(controlled_buffer_6_out), .clk(C), .din(DIn), .dout(ram_3_dout));
  assign controlled_buffer_5_out = demultiplexer_2_out2 ? Address[23:0] : 24'bz;  // Controlled_Buffer controlled_buffer_5
  assign controlled_buffer_6_out = demultiplexer_2_out2 ? En : 1'bz;  // Controlled_Buffer controlled_buffer_6
  assign controlled_buffer_7_out = demultiplexer_2_out3 ? Address[23:0] : 24'bz;  // Controlled_Buffer controlled_buffer_7
  assign controlled_buffer_8_out = demultiplexer_2_out3 ? En : 1'bz;  // Controlled_Buffer controlled_buffer_8
  RAM #(.addrWidth(24), .dataWidth(32), .enables("line")) ram_4 (
    .addr(controlled_buffer_7_out), .we(controlled_buffer_8_out), .clk(C), .din(DIn), .dout(ram_4_dout));
  RAM #(.addrWidth(24), .dataWidth(32), .enables("line")) ram_5 (
    .addr(controlled_buffer_9_out), .we(controlled_buffer_10_out), .clk(C), .din(DIn), .dout(ram_5_dout));
  assign controlled_buffer_9_out = demultiplexer_2_out4 ? Address[23:0] : 24'bz;  // Controlled_Buffer controlled_buffer_9
  assign controlled_buffer_10_out = demultiplexer_2_out4 ? En : 1'bz;  // Controlled_Buffer controlled_buffer_10
  RAM #(.addrWidth(24), .dataWidth(32), .enables("line")) ram_6 (
    .addr(controlled_buffer_11_out), .we(controlled_buffer_12_out), .clk(C), .din(DIn), .dout(ram_6_dout));
  assign controlled_buffer_11_out = demultiplexer_2_out5 ? Address[23:0] : 24'bz;  // Controlled_Buffer controlled_buffer_11
  assign controlled_buffer_12_out = demultiplexer_2_out5 ? En : 1'bz;  // Controlled_Buffer controlled_buffer_12
  RAM #(.addrWidth(24), .dataWidth(32), .enables("line")) ram_7 (
    .addr(controlled_buffer_13_out), .we(controlled_buffer_14_out), .clk(C), .din(DIn), .dout(ram_7_dout));
  assign controlled_buffer_13_out = demultiplexer_2_out6 ? Address[23:0] : 24'bz;  // Controlled_Buffer controlled_buffer_13
  assign controlled_buffer_14_out = demultiplexer_2_out6 ? En : 1'bz;  // Controlled_Buffer controlled_buffer_14
  assign controlled_buffer_15_out = demultiplexer_2_out7 ? En : 1'bz;  // Controlled_Buffer controlled_buffer_15
  RAM #(.addrWidth(24), .dataWidth(32), .enables("line")) ram_8 (
    .addr(controlled_buffer_16_out), .we(controlled_buffer_15_out), .clk(C), .din(DIn), .dout(ram_8_dout));
  assign controlled_buffer_16_out = demultiplexer_2_out7 ? Address[23:0] : 24'bz;  // Controlled_Buffer controlled_buffer_16
  Multiplexer #(.select(5), .width(32)) multiplexer_1 (
    .in0(ram_1_dout), .in1(ram_2_dout), .in2(ram_3_dout), .in3(ram_4_dout), .in4(ram_5_dout),
    .in5(ram_6_dout), .in6(ram_7_dout), .in7(ram_8_dout), .out(multiplexer_1_out), .sel(Address[28:24]));  // open: in8, in9, in10, in11, in12, in13, in14, in15, in16, in17, in18, in19, in20, in21, in22, in23, in24, in25, in26, in27, in28, in29, in30, in31
  Multiplexer #(.select(5), .width(32)) multiplexer_2 (
    .out(multiplexer_2_out), .sel(Address[28:24]));  // open: in0, in1, in2, in3, in4, in5, in6, in7, in8, in9, in10, in11, in12, in13, in14, in15, in16, in17, in18, in19, in20, in21, in22, in23, in24, in25, in26, in27, in28, in29, in30, in31
  Multiplexer #(.width(32)) multiplexer_3 (
    .in0(multiplexer_1_out), .in1(multiplexer_2_out), .out(DOut), .sel(Address[29]));

  // Other names for the same wires on the sheet: Address_t[23:0] = Address[23:0]; ASignal[4:0] = Address[28:24];
  //   ASig = Address[29]
endmodule

module AdrresSelector (
  input  [31:0] Address
);

  wire [23:0] demultiplexer_1_out0, demultiplexer_1_out1;

  Demultiplexer #(.width(24)) demultiplexer_1 (
    .out0(demultiplexer_1_out0), .out1(demultiplexer_1_out1), .sel(Address[29]));  // open: in
  Demultiplexer #(.select(5), .width(24)) demultiplexer_2 (
    .in(demultiplexer_1_out0), .sel(Address[28:24]));  // open: out0, out1, out2, out3, out4, out5, out6, out7, out8, out9, out10, out11, out12, out13, out14, out15, out16, out17, out18, out19, out20, out21, out22, out23, out24, out25, out26, out27, out28, out29, out30, out31
  Demultiplexer #(.select(5), .width(24)) demultiplexer_3 (
    .in(demultiplexer_1_out1), .sel(Address[28:24]));  // open: out0, out1, out2, out3, out4, out5, out6, out7, out8, out9, out10, out11, out12, out13, out14, out15, out16, out17, out18, out19, out20, out21, out22, out23, out24, out25, out26, out27, out28, out29, out30, out31

  // Other names for the same wires on the sheet: ASignal[4:0] = Address[28:24]
endmodule
