// Logisim project InstructionDecoder.circ as structural Verilog: 5 circuits, main circuit InstructionDecoder
module InstructionDecoder (
  input  [31:0] instruction,
  output R,
  output I,
  output S,
  output U,
  output J,
  output B,
  output add,
  output sub,
  output op_sll,
  output op_slt,
  output op_sltu,
  output op_xor,
  output op_srl,
  output op_sra,
  output op_or,
  output op_and,
  output addi,
  output slli,
  output slti,
  output sltiu,
  output xori,
  output srli,
  output srai,
  output ori,
  output andi,
  output lb,
  output lh,
  output lw,
  output lbu,
  output lhu,
  output sb,
  output sh,
  output sw,
  output beq,
  output bne,
  output blt,
  output bge,
  output bltu,
  output bgeu,
  output jal,
  output jalr,
  output lui,
  output auipc,
  output ecall,
  output ebreak,
  output mul,
  output mulh,
  output mulsu,
  output mulu,
  output div,
  output divu,
  output op_rem,
  output remu,
  output [4:0] rd,
  output [4:0] rs1,
  output [4:0] rs2,
  output [31:0] imm
);

  swirl swirl_1 (
    .funct7(instruction[31:25]), .rs2(instruction[24:20]), .rs1(instruction[19:15]),
    .funct3(instruction[14:12]), .rd(instruction[11:7]), .B(B), .I(I), .S(S), .J(J), .U(U), .imm(imm));
  OpcodeDecoder opcodedecoder_1 (
    .funct3(instruction[14:12]), .opcode(instruction[6:0]), .funct7(instruction[31:25]),
    .rs2(instruction[24:20]), .lb(lb), .lh(lh), .lw(lw), .S(S), .lbu(lbu), .lhu(lhu), .sb(sb), .sh(sh),
    .sw(sw), .U(U), .bne(bne), .blt(blt), .bge(bge), .J(J), .bltu(bltu), .bgeu(bgeu), .jal(jal), .B(B),
    .jalr(jalr), .lui(lui), .auipc(auipc), .ecall(ecall), .ebreak(ebreak), .mul(mul), .mulh(mulh),
    .mulsu(mulsu), .mulu(mulu), .div(div), .divu(divu), .op_rem(op_rem), .remu(remu), .R(R), .I(I),
    .beq(beq), .add(add), .sub(sub), .op_sll(op_sll), .op_slt(op_slt), .op_sltu(op_sltu), .op_xor(op_xor),
    .op_srl(op_srl), .op_sra(op_sra), .op_or(op_or), .op_and(op_and), .addi(addi), .slli(slli), .slti(slti),
    .sltiu(sltiu), .xori(xori), .srli(srli), .srai(srai), .ori(ori), .andi(andi));

  assign rd = instruction[11:7];
  assign rs1 = instruction[19:15];
  assign rs2 = instruction[24:20];

  // Other names for the same wires on the sheet: opcode[6:0] = instruction[6:0]; funct3[2:0] = instruction[14:12];
  //   funct7[6:0] = instruction[31:25]
endmodule

module swirl (
  input  [6:0] funct7,
  input  [4:0] rs2,
  input  [4:0] rs1,
  input  [2:0] funct3,
  input  [4:0] rd,
  input  B,
  input  I,
  input  S,
  input  J,
  input  U,
  output [31:0] imm
);

  wire undriven;
  wire [2:0] priority_encoder_1_out;
  wire [31:0] B_t, I_t, J_t, S_t;

  assign I_t = {{20{funct7[6]}}, {funct7, rs2}};  // Bit_Extender bit_extender_1
  // NoConnect on nothing
  assign B_t = {{19{funct7[6]}}, {funct7[6], rd[0], funct7[5:0], rd[4:1], 1'b0}};  // Bit_Extender bit_extender_2
  Multiplexer #(.select(3), .width(32)) multiplexer_1 (
    .in0({32{1'b0}}), .in1(B_t), .in2(I_t), .in3(S_t), .in4(J_t),
    .in5({funct7, rs2, rs1, funct3, {12{1'b0}}}), .in6({32{1'b0}}), .in7({32{1'b0}}), .out(imm),
    .sel(priority_encoder_1_out));
  // NoConnect on nothing
  Priority_Encoder priority_encoder_1 (
    .in0(1'b0), .in1(B), .in2(I), .in3(S), .in4(J), .in5(U), .in6(1'b0), .in7(1'b0),
    .out(priority_encoder_1_out), .en_in(undriven));
  // NoConnect on undriven
  assign S_t = {{20{funct7[6]}}, {funct7, rd}};  // Bit_Extender bit_extender_3
  assign J_t = {{11{funct7[6]}}, {funct7[6], rs1, funct3, rs2[0], funct7[5:0], rs2[4:1], 1'b0}};  // Bit_Extender bit_extender_4

  // Other names for the same wires on the sheet: U_t[31:12] = {funct7, rs2, rs1, funct3};
  //   Uimm[19:0] = {funct7, rs2, rs1, funct3}

  // Notes on the sheet:
  //   imm: pull=down
  //   I
  //   B
  //   S
  //   J
endmodule

module OpcodeDecoder (
  input  [6:0] opcode,
  input  [2:0] funct3,
  input  [6:0] funct7,
  input  [4:0] rs2,
  output R,
  output I,
  output S,
  output U,
  output J,
  output B,
  output add,
  output sub,
  output op_sll,
  output op_slt,
  output op_sltu,
  output op_xor,
  output op_srl,
  output op_sra,
  output op_or,
  output op_and,
  output addi,
  output slli,
  output slti,
  output sltiu,
  output xori,
  output srli,
  output srai,
  output ori,
  output andi,
  output lb,
  output lh,
  output lw,
  output lbu,
  output lhu,
  output sb,
  output sh,
  output sw,
  output beq,
  output bne,
  output blt,
  output bge,
  output bltu,
  output bgeu,
  output jal,
  output jalr,
  output lui,
  output auipc,
  output ecall,
  output ebreak,
  output mul,
  output mulh,
  output mulsu,
  output mulu,
  output div,
  output divu,
  output op_rem,
  output remu
);

  wire and_1_out, demultiplexer_1_out0, demultiplexer_1_out1, demultiplexer_1_out2, demultiplexer_1_out3,
       demultiplexer_1_out4, demultiplexer_1_out5, demultiplexer_1_out6, demultiplexer_1_out7,
       demultiplexer_2_out1, demultiplexer_2_out5, demultiplexer_3_out3, demultiplexer_3_out6,
       demultiplexer_3_out7, demultiplexer_4_out3, demultiplexer_4_out4, demultiplexer_4_out5,
       demultiplexer_4_out6, demultiplexer_4_out7, demultiplexer_5_out2, demultiplexer_5_out3, f7_00, f7_01,
       f7_20, I1, I2, I4;

  PLA #(.in_width(7), .out_width(10), .\table ("0110011 0000000001\n0010011 0000000010\n0000011 0000000100\n1100111 0000001000\n1110011 0000010000\n1100011 0000100000\n1101111 0001000000\n0110111 0010000000\n0010111 0100000000\n01x0011 1000000000\nxxxxxxx 0000000000\nxxxxxxx 0000000000\nxxxxxxx 0000000000")) pla_1 (
    .in(opcode), .out({S, auipc, lui, J, B, I4, jalr, I2, I1, R}));
  PLA #(.in_width(7), .out_width(3), .\table ("0000000 001\n0000001 010\n0100000 100")) pla_2 (
    .in(funct7), .out({f7_20, f7_01, f7_00}));
  Demultiplexer #(.select(3)) demultiplexer_1 (
    .out0(demultiplexer_1_out0), .out1(demultiplexer_1_out1), .out2(demultiplexer_1_out2),
    .out3(demultiplexer_1_out3), .out4(demultiplexer_1_out4), .out5(demultiplexer_1_out5),
    .out6(demultiplexer_1_out6), .out7(demultiplexer_1_out7), .in(R), .sel(funct3));
  Demultiplexer #(.select(3)) demultiplexer_2 (
    .out0(addi), .out1(demultiplexer_2_out1), .out2(slti), .out3(sltiu), .out4(xori),
    .out5(demultiplexer_2_out5), .out6(ori), .out7(andi), .in(I1), .sel(funct3));
  // NoConnect on demultiplexer_3_out3
  Demultiplexer #(.select(3)) demultiplexer_3 (
    .out0(lb), .out1(lh), .out2(lw), .out3(demultiplexer_3_out3), .out4(lbu), .out5(lhu),
    .out6(demultiplexer_3_out6), .out7(demultiplexer_3_out7), .in(I2), .sel(funct3));
  // NoConnect on demultiplexer_3_out6
  // NoConnect on demultiplexer_3_out7
  Demultiplexer #(.select(3)) demultiplexer_4 (
    .out0(sb), .out1(sh), .out2(sw), .out3(demultiplexer_4_out3), .out4(demultiplexer_4_out4),
    .out5(demultiplexer_4_out5), .out6(demultiplexer_4_out6), .out7(demultiplexer_4_out7), .in(S),
    .sel(funct3));
  Demultiplexer #(.select(3)) demultiplexer_5 (
    .out0(beq), .out1(bne), .out2(demultiplexer_5_out2), .out3(demultiplexer_5_out3), .out4(blt), .out5(bge),
    .out6(bltu), .out7(bgeu), .in(B), .sel(funct3));
  and and_1 (and_1_out, R, f7_01);
  Demultiplexer #(.select(3)) demultiplexer_6 (
    .out0(mul), .out1(mulh), .out2(mulsu), .out3(mulu), .out4(div), .out5(divu), .out6(op_rem), .out7(remu),
    .in(and_1_out), .sel(funct3));
  or or_1 (I, I1, I2, jalr, I4);
  // NoConnect on demultiplexer_4_out3
  // NoConnect on demultiplexer_4_out4
  // NoConnect on demultiplexer_4_out5
  // NoConnect on demultiplexer_4_out6
  // NoConnect on demultiplexer_4_out7
  // NoConnect on demultiplexer_5_out2
  // NoConnect on demultiplexer_5_out3
  Demultiplexer demultiplexer_7 (.out0(ecall), .out1(ebreak), .in(I4), .sel(rs2[0]));
  and and_2 (add, demultiplexer_1_out0, f7_00);
  and and_3 (sub, demultiplexer_1_out0, f7_20);
  and and_4 (op_sll, demultiplexer_1_out1, f7_00);
  and and_5 (op_slt, demultiplexer_1_out2, f7_00);
  and and_6 (op_sltu, demultiplexer_1_out3, f7_00);
  and and_7 (op_xor, demultiplexer_1_out4, f7_00);
  and and_8 (op_srl, demultiplexer_1_out5, f7_00);
  and and_9 (op_sra, demultiplexer_1_out5, f7_20);
  and and_10 (op_or, demultiplexer_1_out6, f7_00);
  and and_11 (op_and, demultiplexer_1_out7, f7_00);
  and and_12 (slli, f7_00, demultiplexer_2_out1);
  and and_13 (srli, demultiplexer_2_out5, f7_00);
  and and_14 (srai, demultiplexer_2_out5, f7_20);
  or or_2 (U, lui, auipc);

  assign jal = J;

  // Other names for the same wires on the sheet: op33 = R; op13 = I1; op03 = I2; I3 = jalr; op67 = jalr; op73 = I4;
  //   op63 = B; op6f = J; op37 = lui; op17 = auipc; op23 = S
endmodule

module control (
  input  R,
  input  I,
  input  S,
  input  U,
  input  J,
  input  B,
  input  add,
  input  sub,
  input  op_sll,
  input  op_slt,
  input  op_sltu,
  input  op_xor,
  input  op_srl,
  input  op_sra,
  input  op_or,
  input  op_and,
  input  addi,
  input  slli,
  input  slti,
  input  sltiu,
  input  xori,
  input  srli,
  input  srai,
  input  ori,
  input  andi,
  input  lb,
  input  lh,
  input  lw,
  input  lbu,
  input  lhu,
  input  sb,
  input  sh,
  input  sw,
  input  beq,
  input  bne,
  input  blt,
  input  bge,
  input  bltu,
  input  bgeu,
  input  jal,
  input  jalr,
  input  lui,
  input  auipc,
  input  ecall,
  input  ebreak,
  input  mul,
  input  mulh,
  input  mulsu,
  input  mulu,
  input  div,
  input  divu,
  input  op_rem,
  input  remu,
  output [5:0] ALUOp,
  output ALUSrc,
  output RegWrite,
  output MemWrite,
  output MemToReg
);

  wire and_1_out, AND_Encode, Equals, L_Shift, OR_Encode, Plus, R_Shift, R_Shift_Signed, Smaller, XOR_Encode;

  or or_1 (ALUOp[4], sub, Smaller, Equals);
  or or_2 (Plus, add, addi, lw, sw, sub, lb, lh, jal, jalr);
  or or_3 (Smaller, op_slt, blt);
  or or_4 (Equals, beq, bne);
  or or_5 (AND_Encode, op_and, andi);
  or or_6 (OR_Encode, op_or, ori);
  or or_7 (XOR_Encode, op_xor, xori);
  or or_8 (L_Shift, op_sll, slli);
  or or_9 (R_Shift, op_srl, srli);
  or or_10 (R_Shift_Signed, op_sra, srai);
  Priority_Encoder #(.select(4)) priority_encoder_1 (
    .in0(1'b1), .in1(Equals), .in2(Smaller), .in3(bge), .in4(Plus), .in8(AND_Encode), .in9(OR_Encode),
    .in11(XOR_Encode), .in12(L_Shift), .in13(R_Shift), .in15(R_Shift_Signed), .out(ALUOp[3:0]));  // open: in5, in6, in7, in10, in14, gs, en_out, en_in
  and and_1 (and_1_out, I, ~ecall, ~ebreak);  // AND_Gate
  not not_1 (ALUSrc, R);
  or or_11 (RegWrite, R, U, J, and_1_out);
  or or_12 (MemToReg, lb, lh, lw, lbu, lhu);

  assign ALUOp[5] = bge;
  assign MemWrite = S;

  // Other names for the same wires on the sheet: BInverted = ALUOp[4]; AInverted = bge

  // Notes on the sheet:
  //   ALUOp: pull=down
endmodule

module InstructionDecoder_Control (
  input  [31:0] instruction,
  output [5:0] ALUOp,
  output AluSrc,
  output RegWrite,
  output MemWrite,
  output MemToReg,
  output [4:0] rd,
  output [4:0] rs1,
  output [4:0] rs2,
  output [31:0] imm
);

  wire instructiondecoder_1_add, instructiondecoder_1_addi, instructiondecoder_1_andi,
       instructiondecoder_1_auipc, instructiondecoder_1_b, instructiondecoder_1_beq,
       instructiondecoder_1_bge, instructiondecoder_1_bgeu, instructiondecoder_1_blt,
       instructiondecoder_1_bltu, instructiondecoder_1_bne, instructiondecoder_1_div,
       instructiondecoder_1_divu, instructiondecoder_1_ebreak, instructiondecoder_1_ecall,
       instructiondecoder_1_i, instructiondecoder_1_j, instructiondecoder_1_jal, instructiondecoder_1_jalr,
       instructiondecoder_1_lb, instructiondecoder_1_lbu, instructiondecoder_1_lh, instructiondecoder_1_lhu,
       instructiondecoder_1_lui, instructiondecoder_1_lw, instructiondecoder_1_mul,
       instructiondecoder_1_mulh, instructiondecoder_1_mulsu, instructiondecoder_1_mulu,
       instructiondecoder_1_op_and, instructiondecoder_1_op_or, instructiondecoder_1_op_rem,
       instructiondecoder_1_op_sll, instructiondecoder_1_op_slt, instructiondecoder_1_op_sltu,
       instructiondecoder_1_op_sra, instructiondecoder_1_op_srl, instructiondecoder_1_op_xor,
       instructiondecoder_1_ori, instructiondecoder_1_r, instructiondecoder_1_remu, instructiondecoder_1_s,
       instructiondecoder_1_sb, instructiondecoder_1_sh, instructiondecoder_1_slli,
       instructiondecoder_1_slti, instructiondecoder_1_sltiu, instructiondecoder_1_srai,
       instructiondecoder_1_srli, instructiondecoder_1_sub, instructiondecoder_1_sw, instructiondecoder_1_u,
       instructiondecoder_1_xori;

  InstructionDecoder instructiondecoder_1 (
    .instruction(instruction), .R(instructiondecoder_1_r), .I(instructiondecoder_1_i),
    .S(instructiondecoder_1_s), .U(instructiondecoder_1_u), .J(instructiondecoder_1_j),
    .B(instructiondecoder_1_b), .add(instructiondecoder_1_add), .sub(instructiondecoder_1_sub),
    .op_sll(instructiondecoder_1_op_sll), .op_slt(instructiondecoder_1_op_slt),
    .op_sltu(instructiondecoder_1_op_sltu), .op_xor(instructiondecoder_1_op_xor),
    .op_srl(instructiondecoder_1_op_srl), .op_sra(instructiondecoder_1_op_sra),
    .op_or(instructiondecoder_1_op_or), .op_and(instructiondecoder_1_op_and),
    .addi(instructiondecoder_1_addi), .slli(instructiondecoder_1_slli), .slti(instructiondecoder_1_slti),
    .sltiu(instructiondecoder_1_sltiu), .xori(instructiondecoder_1_xori), .srli(instructiondecoder_1_srli),
    .srai(instructiondecoder_1_srai), .ori(instructiondecoder_1_ori), .andi(instructiondecoder_1_andi),
    .lb(instructiondecoder_1_lb), .lh(instructiondecoder_1_lh), .lw(instructiondecoder_1_lw),
    .lbu(instructiondecoder_1_lbu), .lhu(instructiondecoder_1_lhu), .sb(instructiondecoder_1_sb),
    .sh(instructiondecoder_1_sh), .sw(instructiondecoder_1_sw), .beq(instructiondecoder_1_beq),
    .bne(instructiondecoder_1_bne), .blt(instructiondecoder_1_blt), .bge(instructiondecoder_1_bge),
    .bltu(instructiondecoder_1_bltu), .bgeu(instructiondecoder_1_bgeu), .jal(instructiondecoder_1_jal),
    .jalr(instructiondecoder_1_jalr), .lui(instructiondecoder_1_lui), .auipc(instructiondecoder_1_auipc),
    .ecall(instructiondecoder_1_ecall), .ebreak(instructiondecoder_1_ebreak), .mul(instructiondecoder_1_mul),
    .mulh(instructiondecoder_1_mulh), .mulsu(instructiondecoder_1_mulsu), .mulu(instructiondecoder_1_mulu),
    .div(instructiondecoder_1_div), .divu(instructiondecoder_1_divu), .op_rem(instructiondecoder_1_op_rem),
    .remu(instructiondecoder_1_remu), .rd(rd), .rs1(rs1), .rs2(rs2), .imm(imm));
  control control_1 (
    .R(instructiondecoder_1_r), .I(instructiondecoder_1_i), .S(instructiondecoder_1_s),
    .U(instructiondecoder_1_u), .J(instructiondecoder_1_j), .B(instructiondecoder_1_b),
    .add(instructiondecoder_1_add), .sub(instructiondecoder_1_sub), .op_sll(instructiondecoder_1_op_sll),
    .op_slt(instructiondecoder_1_op_slt), .op_sltu(instructiondecoder_1_op_sltu),
    .op_xor(instructiondecoder_1_op_xor), .op_srl(instructiondecoder_1_op_srl),
    .op_sra(instructiondecoder_1_op_sra), .op_or(instructiondecoder_1_op_or),
    .op_and(instructiondecoder_1_op_and), .addi(instructiondecoder_1_addi), .slli(instructiondecoder_1_slli),
    .slti(instructiondecoder_1_slti), .sltiu(instructiondecoder_1_sltiu), .xori(instructiondecoder_1_xori),
    .srli(instructiondecoder_1_srli), .srai(instructiondecoder_1_srai), .ori(instructiondecoder_1_ori),
    .andi(instructiondecoder_1_andi), .lb(instructiondecoder_1_lb), .lh(instructiondecoder_1_lh),
    .lw(instructiondecoder_1_lw), .lbu(instructiondecoder_1_lbu), .lhu(instructiondecoder_1_lhu),
    .sb(instructiondecoder_1_sb), .sh(instructiondecoder_1_sh), .sw(instructiondecoder_1_sw),
    .beq(instructiondecoder_1_beq), .bne(instructiondecoder_1_bne), .blt(instructiondecoder_1_blt),
    .bge(instructiondecoder_1_bge), .bltu(instructiondecoder_1_bltu), .bgeu(instructiondecoder_1_bgeu),
    .jal(instructiondecoder_1_jal), .jalr(instructiondecoder_1_jalr), .lui(instructiondecoder_1_lui),
    .auipc(instructiondecoder_1_auipc), .ecall(instructiondecoder_1_ecall),
    .ebreak(instructiondecoder_1_ebreak), .mul(instructiondecoder_1_mul), .mulh(instructiondecoder_1_mulh),
    .mulsu(instructiondecoder_1_mulsu), .mulu(instructiondecoder_1_mulu), .div(instructiondecoder_1_div),
    .divu(instructiondecoder_1_divu), .op_rem(instructiondecoder_1_op_rem), .remu(instructiondecoder_1_remu),
    .ALUOp(ALUOp), .ALUSrc(AluSrc), .RegWrite(RegWrite), .MemWrite(MemWrite), .MemToReg(MemToReg));
endmodule
