// Logisim project Registers.circ as structural Verilog: 1 circuit, main circuit Registers
module Registers (
  input  [4:0] Rs1,
  input  [4:0] Rs2,
  input  En,
  input  [4:0] Rd,
  input  [31:0] Data_In,
  input  C,
  output [31:0] Rs1Val,
  output [31:0] Rs2Val
);

  wire decoder_1_out0, decoder_1_out1, decoder_1_out2, decoder_1_out3, decoder_1_out4, decoder_1_out5,
       decoder_1_out6, decoder_1_out7, decoder_1_out8, decoder_1_out9, decoder_1_out10, decoder_1_out11,
       decoder_1_out12, decoder_1_out13, decoder_1_out14, decoder_1_out15, decoder_1_out16, decoder_1_out17,
       decoder_1_out18, decoder_1_out19, decoder_1_out20, decoder_1_out21, decoder_1_out22, decoder_1_out23,
       decoder_1_out24, decoder_1_out25, decoder_1_out26, decoder_1_out27, decoder_1_out28, decoder_1_out29,
       decoder_1_out30, decoder_1_out31;
  wire [31:0] R0_q, r1_q, r2_q, r3_q, r4_q, r5_q, r6_q, r7_q, r8_q, r9_q, r10_q, r11_q, r12_q, r13_q, r14_q,
       r15_q, r16_q, r17_q, r18_q, r19_q, r20_q, r21_q, r22_q, r23_q, r24_q, r25_q, r26_q, r27_q, r28_q,
       r29_q, r30_q, r31_q;

  Decoder #(.select(5)) decoder_1 (
    .out0(decoder_1_out0), .out1(decoder_1_out1), .out2(decoder_1_out2), .out3(decoder_1_out3),
    .out4(decoder_1_out4), .out5(decoder_1_out5), .out6(decoder_1_out6), .out7(decoder_1_out7),
    .out8(decoder_1_out8), .out9(decoder_1_out9), .out10(decoder_1_out10), .out11(decoder_1_out11),
    .out12(decoder_1_out12), .out13(decoder_1_out13), .out14(decoder_1_out14), .out15(decoder_1_out15),
    .out16(decoder_1_out16), .out17(decoder_1_out17), .out18(decoder_1_out18), .out19(decoder_1_out19),
    .out20(decoder_1_out20), .out21(decoder_1_out21), .out22(decoder_1_out22), .out23(decoder_1_out23),
    .out24(decoder_1_out24), .out25(decoder_1_out25), .out26(decoder_1_out26), .out27(decoder_1_out27),
    .out28(decoder_1_out28), .out29(decoder_1_out29), .out30(decoder_1_out30), .out31(decoder_1_out31),
    .sel(Rd), .en(En));
  Register #(.width(32)) R0 (.D({32{1'b0}}), .en(decoder_1_out0), .clk(C), .Q(R0_q));  // open: clr
  Register #(.width(32)) r1 (.D(Data_In), .en(decoder_1_out1), .clk(C), .Q(r1_q));  // open: clr
  Register #(.width(32)) r2 (.D(Data_In), .en(decoder_1_out2), .clk(C), .Q(r2_q));  // open: clr
  Register #(.width(32)) r3 (.D(Data_In), .en(decoder_1_out3), .clk(C), .Q(r3_q));  // open: clr
  Register #(.width(32)) r4 (.D(Data_In), .en(decoder_1_out4), .clk(C), .Q(r4_q));  // open: clr
  Register #(.width(32)) r5 (.D(Data_In), .en(decoder_1_out5), .clk(C), .Q(r5_q));  // open: clr
  Register #(.width(32)) r6 (.D(Data_In), .en(decoder_1_out6), .clk(C), .Q(r6_q));  // open: clr
  Register #(.width(32)) r7 (.D(Data_In), .en(decoder_1_out7), .clk(C), .Q(r7_q));  // open: clr
  Register #(.width(32)) r8 (.D(Data_In), .en(decoder_1_out8), .clk(C), .Q(r8_q));  // open: clr
  Register #(.width(32)) r9 (.D(Data_In), .en(decoder_1_out9), .clk(C), .Q(r9_q));  // open: clr
  Register #(.width(32)) r10 (.D(Data_In), .en(decoder_1_out10), .clk(C), .Q(r10_q));  // open: clr
  Register #(.width(32)) r11 (.D(Data_In), .en(decoder_1_out11), .clk(C), .Q(r11_q));  // open: clr
  Register #(.width(32)) r12 (.D(Data_In), .en(decoder_1_out12), .clk(C), .Q(r12_q));  // open: clr
  Register #(.width(32)) r13 (.D(Data_In), .en(decoder_1_out13), .clk(C), .Q(r13_q));  // open: clr
  Register #(.width(32)) r14 (.D(Data_In), .en(decoder_1_out14), .clk(C), .Q(r14_q));  // open: clr
  Register #(.width(32)) r15 (.D(Data_In), .en(decoder_1_out15), .clk(C), .Q(r15_q));  // open: clr
  Register #(.width(32)) r16 (.D(Data_In), .en(decoder_1_out16), .clk(C), .Q(r16_q));  // open: clr
  Register #(.width(32)) r17 (.D(Data_In), .en(decoder_1_out17), .clk(C), .Q(r17_q));  // open: clr
  Register #(.width(32)) r18 (.D(Data_In), .en(decoder_1_out18), .clk(C), .Q(r18_q));  // open: clr
  Register #(.width(32)) r19 (.D(Data_In), .en(decoder_1_out19), .clk(C), .Q(r19_q));  // open: clr
  Register #(.width(32)) r20 (.D(Data_In), .en(decoder_1_out20), .clk(C), .Q(r20_q));  // open: clr
  Register #(.width(32)) r21 (.D(Data_In), .en(decoder_1_out21), .clk(C), .Q(r21_q));  // open: clr
  Register #(.width(32)) r22 (.D(Data_In), .en(decoder_1_out22), .clk(C), .Q(r22_q));  // open: clr
  Register #(.width(32)) r23 (.D(Data_In), .en(decoder_1_out23), .clk(C), .Q(r23_q));  // open: clr
  Register #(.width(32)) r24 (.D(Data_In), .en(decoder_1_out24), .clk(C), .Q(r24_q));  // open: clr
  Register #(.width(32)) r25 (.D(Data_In), .en(decoder_1_out25), .clk(C), .Q(r25_q));  // open: clr
  Register #(.width(32)) r26 (.D(Data_In), .en(decoder_1_out26), .clk(C), .Q(r26_q));  // open: clr
  Register #(.width(32)) r27 (.D(Data_In), .en(decoder_1_out27), .clk(C), .Q(r27_q));  // open: clr
  Register #(.width(32)) r28 (.D(Data_In), .en(decoder_1_out28), .clk(C), .Q(r28_q));  // open: clr
  Register #(.width(32)) r29 (.D(Data_In), .en(decoder_1_out29), .clk(C), .Q(r29_q));  // open: clr
  Register #(.width(32)) r30 (.D(Data_In), .en(decoder_1_out30), .clk(C), .Q(r30_q));  // open: clr
  Register #(.width(32)) r31 (.D(Data_In), .en(decoder_1_out31), .clk(C), .Q(r31_q));  // open: clr
  Multiplexer #(.select(5), .width(32)) multiplexer_1 (
    .in0(R0_q), .in1(r1_q), .in2(r2_q), .in3(r3_q), .in4(r4_q), .in5(r5_q), .in6(r6_q), .in7(r7_q),
    .in8(r8_q), .in9(r9_q), .in10(r10_q), .in11(r11_q), .in12(r12_q), .in13(r13_q), .in14(r14_q),
    .in15(r15_q), .in16(r16_q), .in17(r17_q), .in18(r18_q), .in19(r19_q), .in20(r20_q), .in21(r21_q),
    .in22(r22_q), .in23(r23_q), .in24(r24_q), .in25(r25_q), .in26(r26_q), .in27(r27_q), .in28(r28_q),
    .in29(r29_q), .in30(r30_q), .in31(r31_q), .out(Rs1Val), .sel(Rs1));
  Multiplexer #(.select(5), .width(32)) multiplexer_2 (
    .in0(R0_q), .in1(r1_q), .in2(r2_q), .in3(r3_q), .in4(r4_q), .in5(r5_q), .in6(r6_q), .in7(r7_q),
    .in8(r8_q), .in9(r9_q), .in10(r10_q), .in11(r11_q), .in12(r12_q), .in13(r13_q), .in14(r14_q),
    .in15(r15_q), .in16(r16_q), .in17(r17_q), .in18(r18_q), .in19(r19_q), .in20(r20_q), .in21(r21_q),
    .in22(r22_q), .in23(r23_q), .in24(r24_q), .in25(r25_q), .in26(r26_q), .in27(r27_q), .in28(r28_q),
    .in29(r29_q), .in30(r30_q), .in31(r31_q), .out(Rs2Val), .sel(Rs2));
endmodule
